// Logisim project CPU.circ as structural Verilog: 8 circuits, main circuit ExampleConfigurationROM
module MCU (
  input  IO_ENABLE,
  input  [7:0] IN,
  input  CLK,
  input  RST,
  output IO_ACTIVE,
  output WRITE_ACTIVE,
  output [7:0] OUT,
  output [7:0] ADDR
);

  wire alu_1_flag, and_1_out, and_2_out, isd_1_address_mux, isd_1_alu_state, isd_1_branch,
       isd_1_memory_select, isd_1_pop, isd_1_push;
  wire [1:0] isd_1_a__r, isd_1_b__r, isd_1_c__w, isd_1_gpr_mux;
  wire [2:0] isd_1_alu_op;
  wire [3:0] isd_1_dynamic_op;
  wire [7:0] gpr_1_out_7, gpr_1_out_8, isd_1_imm_value, isd_1_mem_pointer, multiplexer_2_out,
       multiplexer_3_out, pc_1_out_6, pc_1_out_7, ram_1_data, stk_1_out_6;

  STK stk_1 (.out_6(stk_1_out_6), .in_1(OUT), .in_2(CLK), .in_4(isd_1_pop), .in_5(isd_1_push), .in_3(RST));
  ISD isd_1 (
    .DATA(multiplexer_3_out), .CLK(CLK), .RST(RST), .ALU_OP(isd_1_alu_op), .GPR_MUX(isd_1_gpr_mux),
    .Address_MUX(isd_1_address_mux), .POP(isd_1_pop), .PUSH(isd_1_push), .A__R(isd_1_a__r),
    .B__R(isd_1_b__r), .C__W(isd_1_c__w), .Write_Enable(WRITE_ACTIVE), .BRANCH(isd_1_branch),
    .JMP_FLAG(alu_1_flag), .ALU_OUTPUT(OUT), .MEM_POINTER(isd_1_mem_pointer), .PC_ADDRESS(pc_1_out_7),
    .IMM_VALUE(isd_1_imm_value), .Dynamic_OP(isd_1_dynamic_op), .ALU_State(isd_1_alu_state),
    .Memory_Select(isd_1_memory_select), .External_Address_Select(IO_ACTIVE));
  PC pc_1 (
    .Jump_Address(multiplexer_3_out), .Jump_Enable(isd_1_branch), .out_6(pc_1_out_6), .in_5(RST),
    .out_7(pc_1_out_7), .in_3(isd_1_address_mux), .in_4(CLK));
  Multiplexer #(.width(8), .enable("false")) multiplexer_1 (
    .in0(pc_1_out_6), .in1(isd_1_mem_pointer), .out(ADDR), .sel(isd_1_address_mux));
  Multiplexer #(.select(2), .width(8), .enable("false")) multiplexer_2 (
    .in0(OUT), .in1(multiplexer_3_out), .in2(stk_1_out_6), .in3(isd_1_imm_value), .out(multiplexer_2_out),
    .sel(isd_1_gpr_mux));
  ALU alu_1 (
    .out_6(OUT), .STATIC_OPCODE(isd_1_alu_op), .in_1(gpr_1_out_7), .in_2(gpr_1_out_8), .FLAG(alu_1_flag),
    .DYN_OP(isd_1_dynamic_op), .ALU_STATE(isd_1_alu_state));
  GPR gpr_1 (
    .in_2(isd_1_c__w), .in_3(multiplexer_2_out), .out_7(gpr_1_out_7), .out_8(gpr_1_out_8), .in_5(isd_1_b__r),
    .in_6(isd_1_a__r), .in_1(CLK), .in_4(RST));
  and and_1 (and_1_out, WRITE_ACTIVE, CLK);
  RAM #(.bus("separate")) ram_1 (
    .addr(ADDR), .din(OUT), .data(ram_1_data), .sel(1'b1), .clk(and_1_out), .clr(RST));  // open: str, ld
  Multiplexer #(.width(8), .enable("false")) multiplexer_3 (
    .in0(ram_1_data), .in1(IN), .out(multiplexer_3_out), .sel(and_2_out));
  and and_2 (and_2_out, ~isd_1_memory_select, IO_ENABLE);  // AND_Gate

  // Notes on the sheet:
  //   OUT: pull=down
  //   RST: pull=down
  //   ADDR: pull=down
  //   CLK: pull=down
  //   IN: pull=down
  //   IO_ENABLE: pull=down
  //   TISCv1.3
endmodule

module ALU (
  input  [7:0] in_1,
  input  [7:0] in_2,
  input  [2:0] STATIC_OPCODE,
  input  ALU_STATE,
  input  [3:0] DYN_OP,
  output [7:0] out_6,
  output FLAG
);

  wire and_1_out, and_2_out, and_3_out, and_4_out, and_5_out, and_6_out, and_7_out, and_8_out, and_9_out,
       and_10_out, and_11_out, and_12_out, and_13_out, and_14_out, and_15_out, and_16_out, and_17_out,
       and_18_out, and_19_out, and_20_out, and_21_out, and_22_out, and_23_out, and_24_out, and_25_out,
       and_26_out, and_27_out, and_28_out, and_29_out, and_30_out, and_31_out, and_32_out, and_33_out, CC,
       CI, comparator_1_gt, FC, nA, nB, nor_1_out, nor_2_out, nor_3_out, nor_4_out, nor_5_out, nor_6_out,
       nor_7_out, nor_8_out, o0, o1, o2, o3, o4, o5, o6, o7, OR, or_1_out, or_2_out, or_3_out, or_4_out,
       or_5_out, or_6_out, or_7_out, or_8_out, or_9_out, or_10_out, or_11_out, or_12_out, or_13_out,
       or_14_out, or_15_out, or_16_out, or_17_out, or_18_out, or_19_out, or_20_out, or_21_out, or_22_out,
       or_23_out, or_24_out, or_25_out, or_26_out, xor_1_out, xor_2_out, xor_3_out, xor_4_out, xor_5_out,
       xor_6_out, xor_7_out, xor_8_out, xor_9_out, xor_10_out, xor_11_out, xor_12_out, xor_13_out,
       xor_14_out, xor_15_out, xor_16_out;
  wire [2:0] multiplexer_3_out, rom_1_data;
  wire [3:0] bitadder_1_out, bitadder_2_out;
  wire [6:3] rom_1_data_2;
  wire [7:0] multiplexer_4_out, multiplexer_5_out, multiplexer_6_out, shifter_1_out, shifter_2_out;

  xor xor_1 (xor_1_out, in_1[0], nB);
  xor xor_2 (xor_2_out, in_2[0], nA);
  xor xor_3 (xor_3_out, in_1[1], nB);
  xor xor_4 (xor_4_out, in_2[1], nA);
  xor xor_5 (xor_5_out, in_1[2], nB);
  xor xor_6 (xor_6_out, in_2[2], nA);
  xor xor_7 (xor_7_out, in_1[3], nB);
  xor xor_8 (xor_8_out, in_2[3], nA);
  xor xor_9 (xor_9_out, in_1[4], nB);
  xor xor_10 (xor_10_out, in_2[4], nA);
  xor xor_11 (xor_11_out, in_1[5], nB);
  xor xor_12 (xor_12_out, in_2[5], nA);
  xor xor_13 (xor_13_out, in_1[6], nB);
  xor xor_14 (xor_14_out, in_2[6], nA);
  xor xor_15 (xor_15_out, in_1[7], nB);
  xor xor_16 (xor_16_out, in_2[7], nA);
  nor nor_1 (nor_1_out, xor_1_out, xor_2_out);
  or or_1 (or_1_out, nor_1_out, and_2_out);
  and and_1 (and_1_out, xor_1_out, xor_2_out);
  and and_2 (and_2_out, and_1_out, ~OR);  // AND_Gate
  or or_2 (or_2_out, and_25_out, FC);
  and and_3 (and_3_out, and_2_out, ~CC);  // AND_Gate
  or or_3 (or_3_out, and_3_out, or_2_out);
  nor nor_2 (nor_2_out, xor_3_out, xor_4_out);
  or or_4 (or_4_out, nor_2_out, and_5_out);
  and and_4 (and_4_out, xor_3_out, xor_4_out);
  and and_5 (and_5_out, and_4_out, ~OR);  // AND_Gate
  or or_5 (or_5_out, and_26_out, FC);
  and and_6 (and_6_out, and_5_out, ~CC);  // AND_Gate
  or or_6 (or_6_out, and_6_out, or_5_out);
  nor nor_3 (nor_3_out, xor_5_out, xor_6_out);
  or or_7 (or_7_out, nor_3_out, and_8_out);
  and and_7 (and_7_out, xor_5_out, xor_6_out);
  and and_8 (and_8_out, and_7_out, ~OR);  // AND_Gate
  and and_9 (and_9_out, and_8_out, ~CC);  // AND_Gate
  or or_8 (or_8_out, and_27_out, FC);
  or or_9 (or_9_out, and_9_out, or_8_out);
  nor nor_4 (nor_4_out, xor_7_out, xor_8_out);
  or or_10 (or_10_out, nor_4_out, and_11_out);
  and and_10 (and_10_out, xor_7_out, xor_8_out);
  and and_11 (and_11_out, and_10_out, ~OR);  // AND_Gate
  and and_12 (and_12_out, and_11_out, ~CC);  // AND_Gate
  or or_11 (or_11_out, and_28_out, FC);
  or or_12 (or_12_out, and_12_out, or_11_out);
  nor nor_5 (nor_5_out, xor_9_out, xor_10_out);
  or or_13 (or_13_out, nor_5_out, and_14_out);
  and and_13 (and_13_out, xor_9_out, xor_10_out);
  and and_14 (and_14_out, and_13_out, ~OR);  // AND_Gate
  and and_15 (and_15_out, and_14_out, ~CC);  // AND_Gate
  or or_14 (or_14_out, and_29_out, FC);
  or or_15 (or_15_out, and_15_out, or_14_out);
  nor nor_6 (nor_6_out, xor_11_out, xor_12_out);
  or or_16 (or_16_out, nor_6_out, and_17_out);
  and and_16 (and_16_out, xor_11_out, xor_12_out);
  and and_17 (and_17_out, and_16_out, ~OR);  // AND_Gate
  and and_18 (and_18_out, and_17_out, ~CC);  // AND_Gate
  or or_17 (or_17_out, and_30_out, FC);
  or or_18 (or_18_out, and_18_out, or_17_out);
  nor nor_7 (nor_7_out, xor_13_out, xor_14_out);
  or or_19 (or_19_out, nor_7_out, and_20_out);
  and and_19 (and_19_out, xor_13_out, xor_14_out);
  and and_20 (and_20_out, and_19_out, ~OR);  // AND_Gate
  or or_20 (or_20_out, and_31_out, FC);
  and and_21 (and_21_out, and_20_out, ~CC);  // AND_Gate
  or or_21 (or_21_out, and_21_out, or_20_out);
  nor nor_8 (nor_8_out, xor_15_out, xor_16_out);
  or or_22 (or_22_out, nor_8_out, and_23_out);
  and and_22 (and_22_out, xor_15_out, xor_16_out);
  and and_23 (and_23_out, and_22_out, ~OR);  // AND_Gate
  and and_24 (and_24_out, and_23_out, ~CC);  // AND_Gate
  or or_23 (or_23_out, and_32_out, FC);
  or or_24 (or_24_out, and_24_out, or_23_out);
  xnor xnor_1 (o0, CI, or_1_out);
  and and_25 (and_25_out, CI, ~or_1_out);  // AND_Gate
  xnor xnor_2 (o1, or_3_out, or_4_out);
  and and_26 (and_26_out, or_3_out, ~or_4_out);  // AND_Gate
  xnor xnor_3 (o2, or_6_out, or_7_out);
  and and_27 (and_27_out, or_6_out, ~or_7_out);  // AND_Gate
  xnor xnor_4 (o3, or_9_out, or_10_out);
  and and_28 (and_28_out, or_9_out, ~or_10_out);  // AND_Gate
  xnor xnor_5 (o4, or_12_out, or_13_out);
  and and_29 (and_29_out, or_12_out, ~or_13_out);  // AND_Gate
  xnor xnor_6 (o5, or_15_out, or_16_out);
  and and_30 (and_30_out, or_15_out, ~or_16_out);  // AND_Gate
  xnor xnor_7 (o6, or_18_out, or_19_out);
  and and_31 (and_31_out, or_18_out, ~or_19_out);  // AND_Gate
  xnor xnor_8 (o7, or_21_out, or_22_out);
  and and_32 (and_32_out, or_21_out, ~or_22_out);  // AND_Gate
  Multiplexer #(.select(2), .enable("false")) multiplexer_1 (
    .in0(or_24_out), .in1(or_26_out), .in2(comparator_1_gt), .in3(1'b0), .out(FLAG), .sel(rom_1_data_2[4:3]));
  Multiplexer #(.width(8), .enable("false")) multiplexer_2 (
    .in0({o7, o6, o5, o4, o3, o2, o1, o0}), .in1(multiplexer_6_out), .out(out_6), .sel(and_33_out));
  and and_33 (and_33_out, or_25_out, ALU_STATE);
  Multiplexer #(.width(3), .enable("false")) multiplexer_3 (
    .in0(STATIC_OPCODE), .in1(rom_1_data), .out(multiplexer_3_out), .sel(ALU_STATE));
  ROM #(.addrWidth(4), .dataWidth(7)) rom_1 (.addr(DYN_OP), .data({rom_1_data_2, rom_1_data}));  // open: sel
  ROM #(.addrWidth(3), .dataWidth(6)) rom_2 (.addr(multiplexer_3_out), .data({nA, nB, OR, CC, CI, FC}), .sel(1'b1));
  or or_25 (or_25_out, rom_1_data_2[5], rom_1_data_2[6]);
  Multiplexer #(.width(8), .enable("false")) multiplexer_4 (
    .in0({8{1'b0}}), .in1(in_2), .out(multiplexer_4_out), .sel(or_25_out));
  Multiplexer #(.width(8), .enable("false")) multiplexer_5 (
    .in0({8{1'b0}}), .in1(in_1), .out(multiplexer_5_out), .sel(or_25_out));
  or or_26 (or_26_out, o0, o1, o2, o3, o4, o5, o6, o7);
  BitAdder bitadder_1 (.in0(multiplexer_4_out), .out(bitadder_1_out));
  Shifter shifter_1 (.in(multiplexer_4_out), .\dist (multiplexer_5_out[2:0]), .out(shifter_1_out));
  Shifter #(.shift("lr")) shifter_2 (.in(multiplexer_4_out), .\dist (multiplexer_5_out[2:0]), .out(shifter_2_out));
  BitAdder bitadder_2 (.in0(multiplexer_6_out), .out(bitadder_2_out));
  Multiplexer #(.width(8), .enable("false")) multiplexer_6 (
    .in0(shifter_1_out), .in1(shifter_2_out), .out(multiplexer_6_out), .sel(rom_1_data_2[6]));
  Comparator #(.width(4)) comparator_1 (.a(bitadder_1_out), .b(bitadder_2_out), .gt(comparator_1_gt));  // open: eq, lt

  // Other names for the same wires on the sheet: A[7:0] = in_2; a0 = in_2[0]; a1 = in_2[1]; a2 = in_2[2];
  //   a3 = in_2[3]; a4 = in_2[4]; a5 = in_2[5]; a6 = in_2[6]; a7 = in_2[7]; B[7:0] = in_1; b0 = in_1[0]; b1 = in_1[1];
  //   b2 = in_1[2]; b3 = in_1[3]; b4 = in_1[4]; b5 = in_1[5]; b6 = in_1[6]; b7 = in_1[7]

  // Notes on the sheet:
  //   Output
  //   Input B
  //   Opcodes
  //   contents of rom_1 (hex, n*v repeats v):
  //   3 7 9 a 6 4 30 50
  //   Input A
  //   contents of rom_2 (hex, n*v repeats v):
  //   8 3b 4 0 2 38 7 12
  //   OPCODES: 000: OR, 001: AND, 010: XOR, 011: ADD, 100: CIN, 101: NAND, 110: XNOR, 111: SUB
endmodule

module GPR (
  input  in_1,
  input  [1:0] in_2,
  input  [7:0] in_3,
  input  in_4,
  input  [1:0] in_5,
  input  [1:0] in_6,
  output [7:0] out_7,
  output [7:0] out_8
);

  wire decoder_1_out0, decoder_1_out1, decoder_1_out2, decoder_1_out3, decoder_2_out1, decoder_2_out2,
       decoder_2_out3, decoder_3_out0, decoder_3_out1, decoder_3_out2, decoder_3_out3;
  wire [1:0] multiplexer_1_out;
  wire [7:0] register_1_q, register_2_q, register_3_q;

  Multiplexer #(.width(2), .enable("false")) multiplexer_1 (
    .in0(2'b00), .in1(in_2), .out(multiplexer_1_out), .sel(in_1));
  Decoder #(.select(2), .enable("false")) decoder_1 (
    .out0(decoder_1_out0), .out1(decoder_1_out1), .out2(decoder_1_out2), .out3(decoder_1_out3), .sel(in_5));
  Decoder #(.select(2), .enable("false")) decoder_2 (
    .out1(decoder_2_out1), .out2(decoder_2_out2), .out3(decoder_2_out3), .sel(multiplexer_1_out));  // open: out0
  Register register_1 (.D(in_3), .en(1'b1), .Q(register_1_q), .clk(decoder_2_out1), .clr(in_4));
  Register register_2 (.D(in_3), .en(1'b1), .Q(register_2_q), .clk(decoder_2_out2), .clr(in_4));
  assign out_7 = decoder_1_out1 ? register_1_q : 8'bz;  // Controlled_Buffer controlled_buffer_1
  assign out_7 = decoder_1_out2 ? register_2_q : 8'bz;  // Controlled_Buffer controlled_buffer_2
  assign out_8 = decoder_3_out2 ? register_2_q : 8'bz;  // Controlled_Buffer controlled_buffer_3
  assign out_8 = decoder_3_out1 ? register_1_q : 8'bz;  // Controlled_Buffer controlled_buffer_4
  Register register_3 (.D(in_3), .en(1'b1), .Q(register_3_q), .clk(decoder_2_out3), .clr(in_4));
  assign out_7 = decoder_1_out3 ? register_3_q : 8'bz;  // Controlled_Buffer controlled_buffer_5
  assign out_7 = decoder_1_out0 ? {8{1'b0}} : 8'bz;  // Controlled_Buffer controlled_buffer_6
  assign out_8 = decoder_3_out3 ? register_3_q : 8'bz;  // Controlled_Buffer controlled_buffer_7
  assign out_8 = decoder_3_out0 ? {8{1'b0}} : 8'bz;  // Controlled_Buffer controlled_buffer_8
  Decoder #(.select(2), .enable("false")) decoder_3 (
    .out0(decoder_3_out0), .out1(decoder_3_out1), .out2(decoder_3_out2), .out3(decoder_3_out3), .sel(in_6));
endmodule

module ISD (
  input  [7:0] DATA,
  input  CLK,
  input  RST,
  input  [7:0] ALU_OUTPUT,
  input  [7:0] PC_ADDRESS,
  input  JMP_FLAG,
  output Write_Enable,
  output ALU_State,
  output [3:0] Dynamic_OP,
  output POP,
  output PUSH,
  output [2:0] ALU_OP,
  output [1:0] GPR_MUX,
  output [1:0] A__R,
  output [1:0] B__R,
  output [1:0] C__W,
  output [7:0] MEM_POINTER,
  output [7:0] IMM_VALUE,
  output Memory_Select,
  output Address_MUX,
  output BRANCH,
  output External_Address_Select
);

  wire and_1_out, and_2_out, and_4_out, and_7_out, CIN_out, CMP_out, comparator_1_lt, DYN_out, JMP_out,
       LB_out, LLI_out, LUI_out, NAND_out, or_1_out, or_2_out, or_4_out, OR_5_out, or_6_out, or_8_out,
       or_10_out, or_11_out, or_13_out, or_14_out, or_15_out, or_16_out, or_17_out, or_18_out, or_19_out,
       or_20_out, or_21_out, or_22_out, or_23_out, or_24_out, or_25_out, or_26_out, or_27_out, or_28_out,
       or_29_out, or_30_out, or_31_out, or_32_out, or_34_out, or_35_out, or_36_out, or_37_out, or_40_out,
       or_44_out, PCR_out, POP_out, ptrinc_out, PUSH_out, register_3_q, register_4_q, register_5_q, SOP_out,
       SP_out;
  wire [1:0] multiplexer_3_out, multiplexer_4_out, multiplexer_5_out, multiplexer_8_out, multiplexer_9_out,
       multiplexer_10_out, multiplexer_11_out, multiplexer_12_out, multiplexer_13_out, multiplexer_14_out,
       multiplexer_15_out, multiplexer_16_out, multiplexer_17_out, multiplexer_18_out, multiplexer_19_out,
       multiplexer_20_out, multiplexer_21_out, multiplexer_22_out, multiplexer_23_out;
  wire [3:0] multiplexer_1_out, multiplexer_1_out_2;
  wire [7:0] adder_1_out, multiplexer_2_out, multiplexer_6_out, or_3_out, register_1_q;

  Register #(.trigger("falling")) register_1 (.D(DATA), .Q(register_1_q), .clk(CLK), .clr(RST));  // open: en
  Multiplexer #(.width(8), .enable("false")) multiplexer_1 (
    .in0(register_1_q), .in1({8{1'b0}}), .out({multiplexer_1_out_2, multiplexer_1_out}), .sel(register_4_q));
  Multiplexer #(.width(8), .enable("false")) multiplexer_2 (
    .in0(ALU_OUTPUT), .in1(adder_1_out), .out(multiplexer_2_out), .sel(ptrinc_out));
  Adder adder_1 (.a(8'h1), .b(MEM_POINTER), .out(adder_1_out));  // open: cin, cout
  or or_1 (or_1_out, multiplexer_1_out[2], multiplexer_1_out[3]);
  or or_2 (or_2_out, multiplexer_1_out[2], multiplexer_1_out[3]);
  Multiplexer #(.width(2), .enable("false")) multiplexer_3 (
    .in0(2'b00), .in1(multiplexer_1_out[3:2]), .out(multiplexer_3_out), .sel(or_24_out));
  Multiplexer #(.width(2), .enable("false")) multiplexer_4 (
    .in0(2'b00), .in1(multiplexer_1_out_2[1:0]), .out(multiplexer_4_out), .sel(or_25_out));
  Multiplexer #(.width(2), .enable("false")) multiplexer_5 (
    .in0(2'b00), .in1(multiplexer_1_out_2[3:2]), .out(multiplexer_5_out), .sel(or_29_out));
  assign or_3_out = {multiplexer_1_out_2[1:0], multiplexer_1_out[3:2], 4'b0000} | ALU_OUTPUT;  // OR_Gate or_3, 8 bits wide
  Register register_2 (.D(multiplexer_2_out), .Q(MEM_POINTER), .clk(and_1_out), .clr(RST));  // open: en
  or or_4 (or_4_out, SP_out, ptrinc_out);
  and and_1 (and_1_out, or_4_out, CLK);
  and OR_5 (OR_5_out, ~multiplexer_1_out[0], ~multiplexer_1_out[1], 1'b1, or_1_out, 1'b1, 1'b1, 1'b1, 1'b1);  // AND_Gate
  and SOP (SOP_out, ~multiplexer_1_out[0], ~multiplexer_1_out[1], ~multiplexer_1_out[2], ~multiplexer_1_out[3], 1'b1, 1'b1, 1'b1, 1'b1);  // AND_Gate
  and NAND (NAND_out, multiplexer_1_out[0], ~multiplexer_1_out[1], 1'b1, 1'b1, 1'b1, 1'b1, 1'b1, 1'b1);  // AND_Gate
  or or_6 (or_6_out, NAND_out, 1'b0);
  and DYN (DYN_out, ~multiplexer_1_out[0], multiplexer_1_out[1], 1'b1, or_2_out, 1'b1, 1'b1, 1'b1, 1'b1);  // AND_Gate
  and CIN (CIN_out, ~multiplexer_1_out[0], multiplexer_1_out[1], ~multiplexer_1_out[2], ~multiplexer_1_out[3], 1'b1, 1'b1, 1'b1, 1'b1);  // AND_Gate
  or or_7 (ALU_OP[2], CIN_out, or_6_out);
  and LLI (LLI_out, multiplexer_1_out[0], multiplexer_1_out[1], 1'b1, 1'b1, 1'b1, 1'b1, ~multiplexer_1_out_2[2], ~multiplexer_1_out_2[3]);  // AND_Gate
  and LUI (LUI_out, multiplexer_1_out[0], multiplexer_1_out[1], 1'b1, 1'b1, 1'b1, 1'b1, multiplexer_1_out_2[2], ~multiplexer_1_out_2[3]);  // AND_Gate
  and JMP (JMP_out, multiplexer_1_out[0], multiplexer_1_out[1], ~multiplexer_1_out[2], ~multiplexer_1_out[3], ~multiplexer_1_out_2[0], ~multiplexer_1_out_2[1], ~multiplexer_1_out_2[2], multiplexer_1_out_2[3]);  // AND_Gate
  and u_PUSH (PUSH_out, multiplexer_1_out[0], multiplexer_1_out[1], ~multiplexer_1_out[2], ~multiplexer_1_out[3], multiplexer_1_out_2[0], ~multiplexer_1_out_2[1], ~multiplexer_1_out_2[2], multiplexer_1_out_2[3]);  // AND_Gate
  and u_POP (POP_out, multiplexer_1_out[0], multiplexer_1_out[1], ~multiplexer_1_out[2], ~multiplexer_1_out[3], ~multiplexer_1_out_2[0], multiplexer_1_out_2[1], ~multiplexer_1_out_2[2], multiplexer_1_out_2[3]);  // AND_Gate
  and PCR (PCR_out, multiplexer_1_out[0], multiplexer_1_out[1], ~multiplexer_1_out[2], ~multiplexer_1_out[3], multiplexer_1_out_2[0], multiplexer_1_out_2[1], ~multiplexer_1_out_2[2], multiplexer_1_out_2[3]);  // AND_Gate
  and LB (LB_out, multiplexer_1_out[0], multiplexer_1_out[1], multiplexer_1_out[2], ~multiplexer_1_out[3], 1'b1, 1'b1, ~multiplexer_1_out_2[2], multiplexer_1_out_2[3]);  // AND_Gate
  and SB (Write_Enable, multiplexer_1_out[0], multiplexer_1_out[1], ~multiplexer_1_out[2], multiplexer_1_out[3], 1'b1, 1'b1, ~multiplexer_1_out_2[2], multiplexer_1_out_2[3]);  // AND_Gate
  and SP (SP_out, multiplexer_1_out[0], multiplexer_1_out[1], multiplexer_1_out[2], multiplexer_1_out[3], 1'b1, 1'b1, ~multiplexer_1_out_2[2], multiplexer_1_out_2[3]);  // AND_Gate
  and CMP (CMP_out, multiplexer_1_out[0], multiplexer_1_out[1], 1'b1, 1'b1, 1'b1, 1'b1, multiplexer_1_out_2[2], multiplexer_1_out_2[3]);
  Multiplexer #(.width(8), .enable("false")) multiplexer_6 (
    .in0(or_3_out), .in1({4'b0000, multiplexer_1_out_2[1:0], multiplexer_1_out[3:2]}),
    .out(multiplexer_6_out), .sel(LLI_out));
  or or_8 (or_8_out, NAND_out, 1'b0);
  or or_9 (ALU_OP[1], DYN_out, 1'b0);
  or or_10 (or_10_out, DYN_out, or_8_out);
  and and_2 (and_2_out, LUI_out, ~register_5_q);  // AND_Gate
  or or_11 (or_11_out, and_2_out, or_10_out);
  or or_12 (ALU_OP[0], LB_out, or_11_out);
  Comparator #(.mode("unsigned")) comparator_1 (.a(MEM_POINTER), .b(8'hf0), .lt(comparator_1_lt));  // open: gt, eq
  and and_3 (Memory_Select, comparator_1_lt, Address_MUX);
  or or_13 (or_13_out, OR_5_out, 1'b0);
  or or_14 (or_14_out, OR_5_out, 1'b0);
  or or_15 (or_15_out, NAND_out, or_14_out);
  or or_16 (or_16_out, NAND_out, or_13_out);
  or or_17 (or_17_out, DYN_out, or_16_out);
  or or_18 (or_18_out, DYN_out, or_15_out);
  or or_19 (or_19_out, CIN_out, or_18_out);
  or or_20 (or_20_out, CIN_out, or_17_out);
  or or_21 (or_21_out, LB_out, or_20_out);
  or or_22 (or_22_out, Write_Enable, or_21_out);
  or or_23 (or_23_out, SP_out, or_22_out);
  or or_24 (or_24_out, CMP_out, or_19_out);
  or or_25 (or_25_out, CMP_out, or_23_out);
  Multiplexer #(.width(8), .enable("false")) multiplexer_7 (
    .in0(multiplexer_6_out), .in1(PC_ADDRESS), .out(IMM_VALUE), .sel(PCR_out));
  or or_26 (or_26_out, OR_5_out, 1'b0);
  or or_27 (or_27_out, NAND_out, or_26_out);
  or or_28 (or_28_out, DYN_out, or_27_out);
  or or_29 (or_29_out, CIN_out, or_28_out);
  or or_30 (or_30_out, LLI_out, 1'b0);
  or or_31 (or_31_out, LUI_out, or_30_out);
  or or_32 (or_32_out, POP_out, or_31_out);
  or or_33 (GPR_MUX[1], PCR_out, or_32_out);
  or or_34 (or_34_out, LLI_out, 1'b0);
  or or_35 (or_35_out, LUI_out, or_34_out);
  or or_36 (or_36_out, PCR_out, or_35_out);
  or or_37 (or_37_out, LB_out, 1'b0);
  or or_38 (GPR_MUX[0], LB_out, or_36_out);
  or or_39 (Address_MUX, Write_Enable, or_37_out);
  Register #(.width(1), .trigger("falling")) register_3 (
    .D(and_4_out), .Q(register_3_q), .clk(CLK), .clr(RST));  // open: en
  and and_4 (and_4_out, JMP_FLAG, CMP_out);
  or or_40 (or_40_out, JMP_out, 1'b0);
  or or_41 (POP, POP_out, 1'b0);
  and and_5 (BRANCH, or_40_out, ~register_3_q);  // AND_Gate
  Multiplexer #(.width(2), .enable("false")) multiplexer_8 (
    .in0(2'b00), .in1(2'b00), .out(multiplexer_8_out), .sel(LLI_out));
  Multiplexer #(.width(2), .enable("false")) multiplexer_9 (
    .in0(multiplexer_8_out), .in1(2'b00), .out(multiplexer_9_out), .sel(LUI_out));
  or or_42 (PUSH, PUSH_out, 1'b0);
  Multiplexer #(.width(2), .enable("false")) multiplexer_10 (
    .in0(multiplexer_9_out), .in1(2'b01), .out(multiplexer_10_out), .sel(PUSH_out));
  Multiplexer #(.width(2), .enable("false")) multiplexer_11 (
    .in0(multiplexer_10_out), .in1(2'b00), .out(multiplexer_11_out), .sel(POP_out));
  Multiplexer #(.width(2), .enable("false")) multiplexer_12 (
    .in0(multiplexer_11_out), .in1(2'b00), .out(multiplexer_12_out), .sel(PCR_out));
  assign A__R = multiplexer_3_out | multiplexer_12_out;  // OR_Gate or_43, 2 bits wide
  or or_44 (or_44_out, or_40_out, Address_MUX);
  Register #(.width(1), .trigger("falling")) register_4 (
    .D(or_44_out), .Q(register_4_q), .clk(CLK), .clr(RST));  // open: en
  and and_6 (External_Address_Select, ~comparator_1_lt, Address_MUX);  // AND_Gate
  Multiplexer #(.width(2), .enable("false")) multiplexer_13 (
    .in0(2'b00), .in1(2'b00), .out(multiplexer_13_out), .sel(LLI_out));
  Multiplexer #(.width(2), .enable("false")) multiplexer_14 (
    .in0(2'b00), .in1(2'b01), .out(multiplexer_14_out), .sel(LLI_out));
  Multiplexer #(.width(2), .enable("false")) multiplexer_15 (
    .in0(multiplexer_14_out), .in1(2'b01), .out(multiplexer_15_out), .sel(LUI_out));
  Multiplexer #(.width(2), .enable("false")) multiplexer_16 (
    .in0(multiplexer_13_out), .in1(2'b01), .out(multiplexer_16_out), .sel(LUI_out));
  Multiplexer #(.width(2), .enable("false")) multiplexer_17 (
    .in0(multiplexer_16_out), .in1(2'b00), .out(multiplexer_17_out), .sel(PUSH_out));
  Multiplexer #(.width(2), .enable("false")) multiplexer_18 (
    .in0(multiplexer_15_out), .in1(2'b00), .out(multiplexer_18_out), .sel(PUSH_out));
  Multiplexer #(.width(2), .enable("false")) multiplexer_19 (
    .in0(multiplexer_17_out), .in1(2'b00), .out(multiplexer_19_out), .sel(POP_out));
  Multiplexer #(.width(2), .enable("false")) multiplexer_20 (
    .in0(multiplexer_18_out), .in1(2'b01), .out(multiplexer_20_out), .sel(POP_out));
  Multiplexer #(.width(2), .enable("false")) multiplexer_21 (
    .in0(multiplexer_20_out), .in1(2'b11), .out(multiplexer_21_out), .sel(PCR_out));
  Multiplexer #(.width(2), .enable("false")) multiplexer_22 (
    .in0(multiplexer_19_out), .in1(2'b00), .out(multiplexer_22_out), .sel(PCR_out));
  Multiplexer #(.width(2), .enable("false")) multiplexer_23 (
    .in0(multiplexer_5_out), .in1(multiplexer_4_out), .out(multiplexer_23_out), .sel(Address_MUX));
  assign B__R = multiplexer_4_out | multiplexer_22_out;  // OR_Gate or_45, 2 bits wide
  assign C__W = multiplexer_23_out | multiplexer_21_out;  // OR_Gate or_46, 2 bits wide
  Register #(.width(1), .trigger("falling")) register_5 (
    .D(LLI_out), .Q(register_5_q), .clk(CLK), .clr(RST));  // open: en
  or or_47 (ALU_State, DYN_out, CMP_out);
  and ptrinc (ptrinc_out, multiplexer_1_out_2[0], multiplexer_1_out_2[1], multiplexer_1_out_2[2], multiplexer_1_out_2[3], SOP_out);
  Register #(.width(4), .trigger("falling")) register_6 (
    .D(multiplexer_1_out_2), .Q(Dynamic_OP), .clk(and_7_out), .clr(RST));  // open: en
  and and_7 (and_7_out, ~ptrinc_out, ~register_4_q, SOP_out, CLK);  // AND_Gate

  // Notes on the sheet:
  //   This input defines the range of MMIO -->
endmodule

module STK (
  input  [7:0] in_1,
  input  in_2,
  input  in_3,
  input  in_4,
  input  in_5,
  output [7:0] out_6
);

  wire and_1_out, or_1_out;
  wire [7:0] multiplexer_1_out, multiplexer_2_out, multiplexer_3_out, multiplexer_4_out, multiplexer_5_out,
       multiplexer_6_out, multiplexer_7_out, multiplexer_8_out, multiplexer_9_out, multiplexer_10_out,
       multiplexer_11_out, multiplexer_12_out, multiplexer_13_out, multiplexer_14_out, multiplexer_15_out,
       multiplexer_16_out, multiplexer_17_out, multiplexer_18_out, multiplexer_19_out, multiplexer_20_out,
       multiplexer_21_out, multiplexer_22_out, multiplexer_23_out, multiplexer_24_out, multiplexer_25_out,
       multiplexer_26_out, multiplexer_27_out, multiplexer_28_out, multiplexer_29_out, multiplexer_30_out,
       multiplexer_31_out, multiplexer_32_out, register_2_q, register_3_q, register_4_q, register_5_q,
       register_6_q, register_7_q, register_8_q, register_9_q, register_10_q, register_11_q, register_12_q,
       register_13_q, register_14_q, register_15_q, register_16_q, register_17_q, register_18_q,
       register_19_q, register_20_q, register_21_q, register_22_q, register_23_q, register_24_q,
       register_25_q, register_26_q, register_27_q, register_28_q, register_29_q, register_30_q,
       register_31_q, register_32_q;

  and and_1 (and_1_out, in_2, or_1_out);
  or or_1 (or_1_out, in_4, in_5);
  Multiplexer #(.width(8), .enable("false")) multiplexer_1 (
    .in0(register_2_q), .in1(in_1), .out(multiplexer_1_out), .sel(in_5));
  Multiplexer #(.width(8), .enable("false")) multiplexer_2 (
    .in0(register_3_q), .in1(out_6), .out(multiplexer_2_out), .sel(in_5));
  Register register_1 (.D(multiplexer_1_out), .Q(out_6), .clk(and_1_out), .clr(in_3));  // open: en
  Register register_2 (.D(multiplexer_2_out), .Q(register_2_q), .clk(and_1_out), .clr(in_3));  // open: en
  Multiplexer #(.width(8), .enable("false")) multiplexer_3 (
    .in0(register_4_q), .in1(register_2_q), .out(multiplexer_3_out), .sel(in_5));
  Register register_3 (.D(multiplexer_3_out), .Q(register_3_q), .clk(and_1_out), .clr(in_3));  // open: en
  Multiplexer #(.width(8), .enable("false")) multiplexer_4 (
    .in0(register_5_q), .in1(register_3_q), .out(multiplexer_4_out), .sel(in_5));
  Register register_4 (.D(multiplexer_4_out), .Q(register_4_q), .clk(and_1_out), .clr(in_3));  // open: en
  Multiplexer #(.width(8), .enable("false")) multiplexer_5 (
    .in0(register_6_q), .in1(register_4_q), .out(multiplexer_5_out), .sel(in_5));
  Register register_5 (.D(multiplexer_5_out), .Q(register_5_q), .clk(and_1_out), .clr(in_3));  // open: en
  Multiplexer #(.width(8), .enable("false")) multiplexer_6 (
    .in0(register_7_q), .in1(register_5_q), .out(multiplexer_6_out), .sel(in_5));
  Multiplexer #(.width(8), .enable("false")) multiplexer_7 (
    .in0(register_8_q), .in1(register_6_q), .out(multiplexer_7_out), .sel(in_5));
  Register register_6 (.D(multiplexer_6_out), .Q(register_6_q), .clk(and_1_out), .clr(in_3));  // open: en
  Register register_7 (.D(multiplexer_7_out), .Q(register_7_q), .clk(and_1_out), .clr(in_3));  // open: en
  Multiplexer #(.width(8), .enable("false")) multiplexer_8 (
    .in0(register_9_q), .in1(register_7_q), .out(multiplexer_8_out), .sel(in_5));
  Register register_8 (.D(multiplexer_8_out), .Q(register_8_q), .clk(and_1_out), .clr(in_3));  // open: en
  Multiplexer #(.width(8), .enable("false")) multiplexer_9 (
    .in0(register_10_q), .in1(register_8_q), .out(multiplexer_9_out), .sel(in_5));
  Multiplexer #(.width(8), .enable("false")) multiplexer_10 (
    .in0(register_11_q), .in1(register_9_q), .out(multiplexer_10_out), .sel(in_5));
  Register register_9 (.D(multiplexer_9_out), .Q(register_9_q), .clk(and_1_out), .clr(in_3));  // open: en
  Register register_10 (.D(multiplexer_10_out), .Q(register_10_q), .clk(and_1_out), .clr(in_3));  // open: en
  Multiplexer #(.width(8), .enable("false")) multiplexer_11 (
    .in0(register_12_q), .in1(register_10_q), .out(multiplexer_11_out), .sel(in_5));
  Register register_11 (.D(multiplexer_11_out), .Q(register_11_q), .clk(and_1_out), .clr(in_3));  // open: en
  Multiplexer #(.width(8), .enable("false")) multiplexer_12 (
    .in0(register_13_q), .in1(register_11_q), .out(multiplexer_12_out), .sel(in_5));
  Register register_12 (.D(multiplexer_12_out), .Q(register_12_q), .clk(and_1_out), .clr(in_3));  // open: en
  Multiplexer #(.width(8), .enable("false")) multiplexer_13 (
    .in0(register_14_q), .in1(register_12_q), .out(multiplexer_13_out), .sel(in_5));
  Register register_13 (.D(multiplexer_13_out), .Q(register_13_q), .clk(and_1_out), .clr(in_3));  // open: en
  Multiplexer #(.width(8), .enable("false")) multiplexer_14 (
    .in0(register_15_q), .in1(register_13_q), .out(multiplexer_14_out), .sel(in_5));
  Multiplexer #(.width(8), .enable("false")) multiplexer_15 (
    .in0(register_16_q), .in1(register_14_q), .out(multiplexer_15_out), .sel(in_5));
  Register register_14 (.D(multiplexer_14_out), .Q(register_14_q), .clk(and_1_out), .clr(in_3));  // open: en
  Register register_15 (.D(multiplexer_15_out), .Q(register_15_q), .clk(and_1_out), .clr(in_3));  // open: en
  Multiplexer #(.width(8), .enable("false")) multiplexer_16 (
    .in0(register_17_q), .in1(register_15_q), .out(multiplexer_16_out), .sel(in_5));
  Register register_16 (.D(multiplexer_16_out), .Q(register_16_q), .clk(and_1_out), .clr(in_3));  // open: en
  Multiplexer #(.width(8), .enable("false")) multiplexer_17 (
    .in0(register_18_q), .in1(register_16_q), .out(multiplexer_17_out), .sel(in_5));
  Multiplexer #(.width(8), .enable("false")) multiplexer_18 (
    .in0(register_19_q), .in1(register_17_q), .out(multiplexer_18_out), .sel(in_5));
  Register register_17 (.D(multiplexer_17_out), .Q(register_17_q), .clk(and_1_out), .clr(in_3));  // open: en
  Register register_18 (.D(multiplexer_18_out), .Q(register_18_q), .clk(and_1_out), .clr(in_3));  // open: en
  Multiplexer #(.width(8), .enable("false")) multiplexer_19 (
    .in0(register_20_q), .in1(register_18_q), .out(multiplexer_19_out), .sel(in_5));
  Register register_19 (.D(multiplexer_19_out), .Q(register_19_q), .clk(and_1_out), .clr(in_3));  // open: en
  Multiplexer #(.width(8), .enable("false")) multiplexer_20 (
    .in0(register_21_q), .in1(register_19_q), .out(multiplexer_20_out), .sel(in_5));
  Register register_20 (.D(multiplexer_20_out), .Q(register_20_q), .clk(and_1_out), .clr(in_3));  // open: en
  Multiplexer #(.width(8), .enable("false")) multiplexer_21 (
    .in0(register_22_q), .in1(register_20_q), .out(multiplexer_21_out), .sel(in_5));
  Register register_21 (.D(multiplexer_21_out), .Q(register_21_q), .clk(and_1_out), .clr(in_3));  // open: en
  Multiplexer #(.width(8), .enable("false")) multiplexer_22 (
    .in0(register_23_q), .in1(register_21_q), .out(multiplexer_22_out), .sel(in_5));
  Multiplexer #(.width(8), .enable("false")) multiplexer_23 (
    .in0(register_24_q), .in1(register_22_q), .out(multiplexer_23_out), .sel(in_5));
  Register register_22 (.D(multiplexer_22_out), .Q(register_22_q), .clk(and_1_out), .clr(in_3));  // open: en
  Register register_23 (.D(multiplexer_23_out), .Q(register_23_q), .clk(and_1_out), .clr(in_3));  // open: en
  Multiplexer #(.width(8), .enable("false")) multiplexer_24 (
    .in0(register_25_q), .in1(register_23_q), .out(multiplexer_24_out), .sel(in_5));
  Register register_24 (.D(multiplexer_24_out), .Q(register_24_q), .clk(and_1_out), .clr(in_3));  // open: en
  Multiplexer #(.width(8), .enable("false")) multiplexer_25 (
    .in0(register_26_q), .in1(register_24_q), .out(multiplexer_25_out), .sel(in_5));
  Multiplexer #(.width(8), .enable("false")) multiplexer_26 (
    .in0(register_27_q), .in1(register_25_q), .out(multiplexer_26_out), .sel(in_5));
  Register register_25 (.D(multiplexer_25_out), .Q(register_25_q), .clk(and_1_out), .clr(in_3));  // open: en
  Register register_26 (.D(multiplexer_26_out), .Q(register_26_q), .clk(and_1_out), .clr(in_3));  // open: en
  Multiplexer #(.width(8), .enable("false")) multiplexer_27 (
    .in0(register_28_q), .in1(register_26_q), .out(multiplexer_27_out), .sel(in_5));
  Register register_27 (.D(multiplexer_27_out), .Q(register_27_q), .clk(and_1_out), .clr(in_3));  // open: en
  Multiplexer #(.width(8), .enable("false")) multiplexer_28 (
    .in0(register_29_q), .in1(register_27_q), .out(multiplexer_28_out), .sel(in_5));
  Register register_28 (.D(multiplexer_28_out), .Q(register_28_q), .clk(and_1_out), .clr(in_3));  // open: en
  Multiplexer #(.width(8), .enable("false")) multiplexer_29 (
    .in0(register_30_q), .in1(register_28_q), .out(multiplexer_29_out), .sel(in_5));
  Register register_29 (.D(multiplexer_29_out), .Q(register_29_q), .clk(and_1_out), .clr(in_3));  // open: en
  Multiplexer #(.width(8), .enable("false")) multiplexer_30 (
    .in0(register_31_q), .in1(register_29_q), .out(multiplexer_30_out), .sel(in_5));
  Multiplexer #(.width(8), .enable("false")) multiplexer_31 (
    .in0(register_32_q), .in1(register_30_q), .out(multiplexer_31_out), .sel(in_5));
  Register register_30 (.D(multiplexer_30_out), .Q(register_30_q), .clk(and_1_out), .clr(in_3));  // open: en
  Register register_31 (.D(multiplexer_31_out), .Q(register_31_q), .clk(and_1_out), .clr(in_3));  // open: en
  Multiplexer #(.width(8), .enable("false")) multiplexer_32 (
    .in0({8{1'b0}}), .in1(register_31_q), .out(multiplexer_32_out), .sel(in_5));
  Register register_32 (.D(multiplexer_32_out), .Q(register_32_q), .clk(and_1_out), .clr(in_3));  // open: en
endmodule

module PC (
  input  [7:0] Jump_Address,
  input  Jump_Enable,
  input  in_3,
  input  in_4,
  input  in_5,
  output [7:0] out_6,
  output [7:0] out_7
);

  wire not_1_out;
  wire [7:0] multiplexer_1_out;

  Multiplexer #(.width(8), .enable("false")) multiplexer_1 (
    .in0(out_7), .in1(Jump_Address), .out(multiplexer_1_out), .sel(Jump_Enable));
  not not_1 (not_1_out, in_3);
  Register #(.trigger("falling")) register_1 (.D(multiplexer_1_out), .en(not_1_out), .Q(out_6), .clk(in_4), .clr(in_5));
  Adder adder_1 (.a(out_6), .b(8'h1), .out(out_7));  // open: cin, cout
endmodule

module ExampleConfigurationROM (
  input  [7:0] in_1,
  input  [7:0] in_2,
  input  RESET,
  output WRITE_ACTIVE,
  output IO_ACTIVE,
  output IO_ENABLE
);

  wire and_1_out, and_2_out, and_3_out, and_4_out, and_5_out, and_6_out, and_7_out, and_8_out, and_9_out,
       and_10_out, CLOCK_out, comparator_1_gt, comparator_2_eq, comparator_3_eq, comparator_4_eq,
       comparator_5_eq, keyboard_1_avail, or_2_out, or_3_out;
  wire [7:0] controlled_buffer_1_out, controlled_buffer_2_out, keyboard_1_data, mcu_1_addr, mcu_1_out,
       register_1_q, register_2_q, register_3_q, rom_1_data;

  MCU mcu_1 (
    .IO_ENABLE(IO_ENABLE), .IN(controlled_buffer_2_out), .ADDR(mcu_1_addr), .OUT(mcu_1_out), .CLK(CLOCK_out),
    .RST(RESET), .IO_ACTIVE(IO_ACTIVE), .WRITE_ACTIVE(WRITE_ACTIVE));
  or or_1 (IO_ENABLE, or_2_out, and_1_out);
  or or_2 (or_2_out, or_3_out, and_3_out);
  or or_3 (or_3_out, and_5_out, and_4_out);
  Clock CLOCK (.out(CLOCK_out));
  Comparator #(.mode("unsigned")) comparator_1 (.a(8'hfc), .b(mcu_1_addr), .gt(comparator_1_gt));  // open: eq, lt
  Comparator #(.mode("unsigned")) comparator_2 (.a(mcu_1_addr), .b({8{1'b1}}), .eq(comparator_2_eq));  // open: gt, lt
  Comparator #(.mode("unsigned")) comparator_3 (.a(mcu_1_addr), .b(8'hfe), .eq(comparator_3_eq));  // open: gt, lt
  Comparator #(.mode("unsigned")) comparator_4 (.a(mcu_1_addr), .b(8'hfd), .eq(comparator_4_eq));  // open: gt, lt
  Comparator #(.mode("unsigned")) comparator_5 (.a(mcu_1_addr), .b(8'hfc), .eq(comparator_5_eq));  // open: gt, lt
  // Probe on controlled_buffer_2_out
  // Probe on mcu_1_addr
  // Probe on mcu_1_out
  and and_1 (and_1_out, comparator_1_gt, ~IO_ACTIVE);  // AND_Gate
  and and_2 (and_2_out, IO_ACTIVE, comparator_2_eq, WRITE_ACTIVE);
  and and_3 (and_3_out, comparator_3_eq, IO_ACTIVE);
  and and_4 (and_4_out, comparator_4_eq, IO_ACTIVE);
  assign controlled_buffer_1_out = comparator_5_eq ? mcu_1_out : 8'bz;  // Controlled_Buffer controlled_buffer_1
  and and_5 (and_5_out, comparator_5_eq, IO_ACTIVE);
  Register register_1 (.D(mcu_1_out), .en(and_2_out), .Q(register_1_q), .clk(CLOCK_out), .clr(RESET));
  // Probe on {register_1_q, mcu_1_addr}
  Register register_2 (.D(mcu_1_out), .en(and_6_out), .Q(register_2_q), .clk(CLOCK_out), .clr(RESET));
  Hex_Digit_Display hex_digit_display_1 (.value(register_2_q[7:4]));  // open: dp
  and and_6 (and_6_out, and_3_out, WRITE_ACTIVE);
  Register register_3 (.D(mcu_1_out), .en(and_7_out), .Q(register_3_q), .clk(CLOCK_out), .clr(RESET));
  Hex_Digit_Display hex_digit_display_2 (.value(register_3_q[7:4]));  // open: dp
  and and_7 (and_7_out, and_4_out, WRITE_ACTIVE);
  and and_8 (and_8_out, ~controlled_buffer_1_out[7], WRITE_ACTIVE, and_10_out);  // AND_Gate
  and and_9 (and_9_out, controlled_buffer_1_out[7], WRITE_ACTIVE, and_10_out);
  and and_10 (and_10_out, and_5_out, CLOCK_out);
  Hex_Digit_Display hex_digit_display_3 (.value(register_2_q[3:0]));  // open: dp
  Hex_Digit_Display hex_digit_display_4 (.value(register_3_q[3:0]));  // open: dp
  TTY #(.cols(80), .trigger("falling")) tty_1 (
    .data(controlled_buffer_1_out[6:0]), .clk(and_10_out), .we(and_8_out), .clr(RESET));
  Keyboard #(.buflen(80), .trigger("falling")) keyboard_1 (
    .clk(and_10_out), .re(and_9_out), .clr(RESET), .avail(keyboard_1_avail), .data(keyboard_1_data[6:0]));
  ROM #(.addrWidth(16)) rom_1 (.addr({register_1_q, mcu_1_addr}), .data(rom_1_data));  // open: sel
  assign controlled_buffer_2_out = and_1_out ? rom_1_data : 8'bz;  // Controlled_Buffer controlled_buffer_2
  assign controlled_buffer_2_out = and_3_out ? in_1 : 8'bz;  // Controlled_Buffer controlled_buffer_3
  assign controlled_buffer_2_out = and_4_out ? in_2 : 8'bz;  // Controlled_Buffer controlled_buffer_4
  not not_1 (keyboard_1_data[7], keyboard_1_avail);
  assign controlled_buffer_2_out = and_5_out ? keyboard_1_data : 8'bz;  // Controlled_Buffer controlled_buffer_5

  // Notes on the sheet:
  //   Sets the memory-mapped address range
  //   Memory Mapped I/O Port Address
  //   Memory Mapped I/O Port Address
  //   Memory Mapped I/O Port Address
  //   PROGRAM MEMORY
  //   Output:
  //   contents of rom_1 (hex, n*v repeats v):
  //   4b c4 30 33 7f 9f 63 a7 db 83 7 ab 9b 23 e7 83 1e bf ab f2 5f f7 83 0 2b db 83 27 83 2 4b f7 83 2 7
  //   10 de 83 2 4b 9f a7 93 33 7f 9f ab a3 52 f7 83 0 83 28
  //    ← Keyboard
endmodule

module gridtest (
  input  [7:0] in_1,
  input  RESET
);

  wire and_1_out, and_2_out, and_3_out, and_4_out, comparator_1_gt, comparator_2_eq, comparator_3_eq,
       comparator_4_eq, mcu_1_p1, mcu_1_p2, mcu_1_p6, or_2_out;
  wire [7:0] mcu_1_p3, mcu_1_p4, mcu_1_p5, register_1_q, register_2_q, register_3_q, rom_1_data, undriven;

  // MCU mcu_1: pin names not known; wires that end beside it: mcu_1_p1, mcu_1_p2, mcu_1_p3, mcu_1_p4, mcu_1_p5, mcu_1_p6, RESET
  or or_1 (mcu_1_p2, or_2_out, and_1_out);
  or or_2 (or_2_out, and_4_out, and_3_out);
  Clock CLOCK (.out(mcu_1_p6));
  Comparator #(.mode("unsigned")) comparator_1 (.a(8'hfc), .b(mcu_1_p4), .gt(comparator_1_gt));  // open: eq, lt
  Comparator #(.mode("unsigned")) comparator_2 (.a(mcu_1_p4), .b({8{1'b1}}), .eq(comparator_2_eq));  // open: gt, lt
  Comparator #(.mode("unsigned")) comparator_3 (.a(mcu_1_p4), .b(8'hfe), .eq(comparator_3_eq));  // open: gt, lt
  Comparator #(.mode("unsigned")) comparator_4 (.a(mcu_1_p4), .b(8'hfd), .eq(comparator_4_eq));  // open: gt, lt
  // Probe on mcu_1_p3
  // Probe on mcu_1_p4
  // Probe on mcu_1_p5
  and and_1 (and_1_out, comparator_1_gt, ~mcu_1_p1);  // AND_Gate
  and and_2 (and_2_out, mcu_1_p1, comparator_2_eq);
  and and_3 (and_3_out, comparator_3_eq, mcu_1_p1);
  and and_4 (and_4_out, comparator_4_eq, mcu_1_p1);
  Register register_1 (.D(mcu_1_p5), .en(and_2_out), .Q(register_1_q), .clk(mcu_1_p6), .clr(RESET));
  // Probe on {register_1_q, mcu_1_p4}
  Register register_2 (.D(mcu_1_p5), .en(and_3_out), .Q(register_2_q), .clk(mcu_1_p6), .clr(RESET));
  Hex_Digit_Display hex_digit_display_1 (.value(register_2_q[7:4]));  // open: dp
  Register register_3 (.D(mcu_1_p5), .en(and_4_out), .Q(register_3_q), .clk(mcu_1_p6), .clr(RESET));
  assign mcu_1_p3 = and_4_out ? undriven : 8'bz;  // Controlled_Buffer controlled_buffer_1
  Hex_Digit_Display hex_digit_display_2 (.value(register_2_q[3:0]));  // open: dp
  assign mcu_1_p3 = and_3_out ? in_1 : 8'bz;  // Controlled_Buffer controlled_buffer_2
  ROM #(.addrWidth(16)) rom_1 (.addr({register_1_q, mcu_1_p4}), .data(rom_1_data));  // open: sel
  assign mcu_1_p3 = and_1_out ? rom_1_data : 8'bz;  // Controlled_Buffer controlled_buffer_3

  // Notes on the sheet:
  //   Sets the memory-mapped address range
  //   Memory Mapped I/O Port Address
  //   Memory Mapped I/O Port Address
  //   contents of rom_1 (hex, n*v repeats v):
  //   3 4b c4 30 33 7f 9f 3 63 a7 db 83 9 ab 9b 23 43 e7 83 23 bf ab f2 3 5f f7 83 0 2b 43 db 83 2e 83 3 3
  //   4b f7 83 3 7 43 10 de 83 3 3 4b 9f a7 93 33 7f 9f ab a3 52 f7 83 0 83 30
endmodule
